// Logisim project addtractor.circ as structural Verilog: 4 circuits, main circuit main
module main (
  input  [2:0] x,
  input  [2:0] y,
  input  k0,
  input  s_a,
  output [2:0] s,
  output k3
);

  wire [2:0] G, P, Q, xor_2_out;
  wire [2:1] k1_k2;

  assign Q = x ^ y;  // XOR_Gate xor_1, 3 bits wide
  assign P = xor_2_out | y;  // OR_Gate or_1, 3 bits wide
  assign G = xor_2_out & y;  // AND_Gate and_1, 3 bits wide
  assign xor_2_out = x ^ {3{s_a}};  // XOR_Gate xor_2, 3 bits wide
  k1 k1 (.p(P), .g(G), .k0(k0), .k2(k1_k2[1]));
  k2 k2 (.p(P), .g(G), .k0(k0), .k2(k1_k2[2]));
  k3 k3_1 (.p(P), .g(G), .k0(k0), .k3(k3));
  assign s = Q ^ {k1_k2, k0};  // XOR_Gate xor_3, 3 bits wide
endmodule

module k3 (
  input  [2:0] p,
  input  [2:0] g,
  input  k0,
  output k3
);

  wire and_1_out, p2g1_out, p2p1g0_out;

  and p2g1 (p2g1_out, p[2], g[1]);
  and p2p1g0 (p2p1g0_out, p[2], p[1], g[0]);
  and and_1 (and_1_out, p[0], p[1], p[2], k0);
  or or_1 (k3, and_1_out, p2p1g0_out, p2g1_out, g[2]);
endmodule

module k2 (
  input  [2:0] p,
  input  [2:0] g,
  input  k0,
  output k2
);

  wire p1g0_out, p1p0k0_out;

  and p1g0 (p1g0_out, g[0], p[1]);
  and p1p0k0 (p1p0k0_out, p[0], p[1], k0);
  or or_1 (k2, p1p0k0_out, p1g0_out, g[1]);
endmodule

module k1 (
  input  [2:0] p,
  input  [2:0] g,
  input  k0,
  output k2
);

  wire p0k0_out;

  and p0k0 (p0k0_out, k0, p[0]);
  or or_1 (k2, p0k0_out, g[0]);
endmodule
