// Logisim project FourToOneMux.circ as structural Verilog: 5 circuits, main circuit FourToOneMux
module FourToOneMux (
  input  [3:0] X,
  input  [3:0] Y,
  input  [3:0] Z,
  input  [3:0] W,
  input  [1:0] S,
  output [3:0] F
);

  FourByFour fourbyfour_1 ();

  // Notes on the sheet:
  //   Build your mux here.
endmodule

module FourToOneMuxTest (
  input  [3:0] in_1,
  input  [3:0] in_2,
  input  [3:0] in_3,
  input  [3:0] in_4,
  input  [1:0] in_5,
  output [3:0] out_6
);

  FourToOneMux fourtoonemux_1 (.X(in_1), .Y(in_2), .Z(in_3), .W(in_4), .S(in_5), .F(out_6));

  // Notes on the sheet:
  //   Build a circuit to test your mux here.
endmodule

module TwoBitDecoder (
  input  S1,
  input  S0,
  output O1,
  output O2,
  output O3,
  output O4
);

  wire not_1_out, not_2_out;

  not not_1 (not_1_out, S1);
  not not_2 (not_2_out, S0);
  and and_1 (O1, not_1_out, not_2_out);
  and and_2 (O2, not_1_out, S0);
  and and_3 (O2, not_1_out, S0);
  and and_4 (O3, S1, not_2_out);
  and and_5 (O4, S1, S0);
  and and_6 (O4, S1, S0);
endmodule

module FourByOne (
  input  First,
  input  Second,
  input  Third,
  input  Fourth,
  input  b1,
  input  b2,
  input  b3,
  input  b4,
  output F1
);

  wire and_1_out, and_2_out, and_4_out, and_5_out;

  and and_1 (and_1_out, First, b1);
  and and_2 (and_2_out, Second, b2);
  and and_3 (and_2_out, Second, b2);
  and and_4 (and_4_out, Third, b3);
  and and_5 (and_5_out, Fourth, b4);
  and and_6 (and_5_out, Fourth, b4);
  or or_1 (F1, and_1_out, and_2_out, and_4_out, and_5_out);
endmodule

module FourByFour (
);

  wire twobitdecoder_1_o1, twobitdecoder_1_o2, twobitdecoder_1_o3, twobitdecoder_1_o4;
  wire [1:0] S;
  wire [3:0] F, W, X, Y, Z;

  TwoBitDecoder twobitdecoder_1 (
    .S1(S[1]), .S0(S[0]), .O1(twobitdecoder_1_o1), .O2(twobitdecoder_1_o2), .O3(twobitdecoder_1_o3),
    .O4(twobitdecoder_1_o4));
  FourByOne fourbyone_1 (
    .First(X[0]), .Second(Y[0]), .Third(Z[0]), .Fourth(W[0]), .b1(twobitdecoder_1_o1),
    .b2(twobitdecoder_1_o2), .b3(twobitdecoder_1_o3), .b4(twobitdecoder_1_o4), .F1(F[0]));
  FourByOne fourbyone_2 (
    .First(X[1]), .Second(Y[1]), .Third(Z[1]), .Fourth(W[1]), .b1(twobitdecoder_1_o1),
    .b2(twobitdecoder_1_o2), .b3(twobitdecoder_1_o3), .b4(twobitdecoder_1_o4), .F1(F[1]));
  FourByOne fourbyone_3 (
    .First(X[2]), .Second(Y[2]), .Third(Z[2]), .Fourth(W[2]), .b1(twobitdecoder_1_o1),
    .b2(twobitdecoder_1_o2), .b3(twobitdecoder_1_o3), .b4(twobitdecoder_1_o4), .F1(F[2]));
  FourByOne fourbyone_4 (
    .First(X[3]), .Second(Y[3]), .Third(Z[3]), .Fourth(W[3]), .b1(twobitdecoder_1_o1),
    .b2(twobitdecoder_1_o2), .b3(twobitdecoder_1_o3), .b4(twobitdecoder_1_o4), .F1(F[3]));
endmodule
