// Logisim project OneBitFA.circ as structural Verilog: 2 circuits, main circuit OneBitFA
module OneBitFA (
  input  A,
  input  B,
  input  Cin,
  output Cout,
  output S
);

  wire nand_1_out, nand_3_out, nand_4_out, nand_6_out, nand_7_out, nand_9_out, nand_10_out;

  nand nand_1 (nand_1_out, A, B);
  nand nand_2 (nand_1_out, A, B);
  nand nand_3 (nand_3_out, A, nand_1_out);
  nand nand_4 (nand_4_out, nand_1_out, B);
  nand nand_5 (nand_4_out, nand_1_out, B);
  nand nand_6 (nand_6_out, nand_3_out, nand_4_out);
  nand nand_7 (nand_7_out, nand_6_out, Cin);
  nand nand_8 (nand_7_out, nand_6_out, Cin);
  nand nand_9 (nand_9_out, nand_6_out, nand_7_out);
  nand nand_10 (nand_10_out, nand_7_out, Cin);
  nand nand_11 (nand_10_out, nand_7_out, Cin);
  nand nand_12 (Cout, nand_7_out, nand_1_out);
  nand nand_13 (S, nand_9_out, nand_10_out);

  // Notes on the sheet:
  //   Build your one bit Full Adder here
endmodule

module OneBitFATest (
  input  in_1,
  input  in_2,
  input  in_3,
  output out_4,
  output out_5
);

  OneBitFA onebitfa_1 (.A(in_1), .B(in_2), .Cin(in_3), .Cout(out_4), .S(out_5));

  // Notes on the sheet:
  //   Build your adder test ciruit here.
endmodule
