// Logisim project SevenSegmentDigit.circ as structural Verilog: 3 circuits, main circuit SevenSegmentDigit
module SevenSegmentDigit (
  input  [3:0] i,
  output a,
  output b,
  output c,
  output d,
  output e,
  output f,
  output g
);

  _7_Segment_Display u_7_segment_display_1 (.g(g), .f(f), .a(a), .b(b), .e(e), .d(d), .c(c));  // open: dp
  FourToSevenDecoder fourtosevendecoder_1 (
    .A(i[3]), .B(i[2]), .C(i[1]), .D(i[0]), .out_5(a), .out_6(b), .out_7(c), .out_8(d), .out_9(e),
    .out_10(f), .out_11(g));

  // Notes on the sheet:
  //   Build your seven segment decoder here
endmodule

module SevenSegmentDigitTest (
  input  [3:0] in_1
);

  wire a, b, c, d, e, f, g;

  SevenSegmentDigit sevensegmentdigit_1 (.i(in_1), .a(a), .b(b), .c(c), .d(d), .e(e), .f(f), .g(g));
  _7_Segment_Display u_7_segment_display_1 (.g(g), .f(f), .a(a), .b(b), .e(e), .d(d), .c(c));  // open: dp

  // Notes on the sheet:
  //   Build your seven segment decoder test circuit here
endmodule

module FourToSevenDecoder (
  input  A,
  input  B,
  input  C,
  input  D,
  output out_5,
  output out_6,
  output out_7,
  output out_8,
  output out_9,
  output out_10,
  output out_11
);

  wire and_1_out, and_2_out, and_3_out, and_4_out, and_5_out, and_6_out, and_7_out, and_8_out, and_9_out,
       not_1_out, not_2_out, not_3_out;

  not not_1 (not_1_out, B);
  not not_2 (not_2_out, C);
  not not_3 (not_3_out, D);
  and and_1 (and_1_out, B, D);
  and and_2 (and_2_out, not_1_out, not_3_out);
  and and_3 (and_3_out, C, D);
  and and_4 (and_4_out, not_2_out, not_3_out);
  and and_5 (and_5_out, C, not_3_out);
  and and_6 (and_6_out, C, not_1_out);
  and and_7 (and_7_out, not_2_out, D, B);
  and and_8 (and_8_out, not_2_out, B);
  and and_9 (and_9_out, not_3_out, B);
  or or_1 (out_5, and_1_out, and_2_out, C, A);
  or or_2 (out_6, and_3_out, not_1_out, and_4_out);
  or or_3 (out_7, D, not_2_out, B);
  or or_4 (out_8, A, and_2_out, and_5_out, and_6_out, and_7_out);
  or or_5 (out_9, and_5_out, and_2_out);
  or or_6 (out_10, and_4_out, and_9_out, and_8_out, A);
  or or_7 (out_11, A, and_5_out, and_8_out, and_6_out);
endmodule
