// Logisim project SixBitAdder.circ as structural Verilog: 2 circuits, main circuit main
module main (
  input  [5:0] in_1,
  input  [5:0] in_2,
  input  CIN,
  output [5:0] out_4,
  output [5:0] SUM,
  output [5:0] out_6
);

  wire and_1_out, and_2_out, and_3_out, and_4_out, and_5_out, and_6_out, and_7_out, and_8_out, and_9_out,
       and_10_out, and_11_out, and_12_out, and_13_out, and_14_out, and_15_out, and_16_out, and_17_out,
       and_18_out, and_19_out, and_20_out, and_21_out, bitcross_1_g, bitcross_1_p, bitcross_2_g,
       bitcross_2_p, bitcross_3_g, bitcross_3_p, bitcross_4_g, bitcross_4_p, bitcross_5_g, bitcross_5_p,
       bitcross_6_g, bitcross_6_p;

  BitCross bitcross_1 (.A(in_1[0]), .B(in_2[0]), .Cin(CIN), .G(bitcross_1_g), .P(bitcross_1_p), .S(SUM[0]));
  and and_1 (and_1_out, bitcross_1_p, CIN);
  or or_1 (out_4[0], bitcross_1_g, and_1_out);
  BitCross bitcross_2 (.A(in_1[1]), .B(in_2[1]), .Cin(out_4[0]), .G(bitcross_2_g), .P(bitcross_2_p), .S(SUM[1]));
  and and_2 (and_2_out, bitcross_2_p, bitcross_1_g);
  and and_3 (and_3_out, bitcross_2_p, bitcross_1_p, CIN);
  BitCross bitcross_3 (.A(in_1[2]), .B(in_2[2]), .Cin(out_4[1]), .G(bitcross_3_g), .P(bitcross_3_p), .S(SUM[2]));
  or or_2 (out_4[1], bitcross_2_g, and_2_out, and_3_out);
  and and_4 (and_4_out, bitcross_3_p, bitcross_2_g);
  and and_5 (and_5_out, bitcross_3_p, bitcross_2_p, bitcross_1_g);
  and and_6 (and_6_out, bitcross_3_p, bitcross_2_p, bitcross_1_p, CIN);
  BitCross bitcross_4 (.A(in_1[3]), .B(in_2[3]), .Cin(out_4[2]), .G(bitcross_4_g), .P(bitcross_4_p), .S(SUM[3]));
  or or_3 (out_4[2], bitcross_3_g, and_4_out, and_5_out, and_6_out);
  and and_7 (and_7_out, bitcross_4_p, bitcross_3_g);
  and and_8 (and_8_out, bitcross_4_p, bitcross_2_g, bitcross_3_p);
  and and_9 (and_9_out, bitcross_4_p, bitcross_1_g, bitcross_3_p, bitcross_2_p);
  and and_10 (and_10_out, bitcross_4_p, bitcross_3_p, bitcross_2_p, bitcross_1_p, CIN);
  BitCross bitcross_5 (.A(in_1[4]), .B(in_2[4]), .Cin(out_4[3]), .G(bitcross_5_g), .P(bitcross_5_p), .S(SUM[4]));
  or or_4 (out_4[3], bitcross_4_g, and_7_out, and_8_out, and_9_out, and_10_out);
  and and_11 (and_11_out, bitcross_5_p, bitcross_4_g);
  and and_12 (and_12_out, bitcross_5_p, bitcross_3_g, bitcross_4_p);
  and and_13 (and_13_out, bitcross_5_p, bitcross_2_g, bitcross_4_p, bitcross_3_p);
  and and_14 (and_14_out, bitcross_5_p, bitcross_1_g, bitcross_4_p, bitcross_3_p, bitcross_2_p);
  and and_15 (and_15_out, bitcross_5_p, bitcross_4_p, bitcross_3_p, bitcross_2_p, bitcross_1_p, CIN);
  BitCross bitcross_6 (.A(in_1[5]), .B(in_2[5]), .Cin(out_4[4]), .G(bitcross_6_g), .P(bitcross_6_p), .S(SUM[5]));
  or or_5 (out_4[4], bitcross_5_g, and_11_out, and_12_out, and_13_out, and_14_out, and_15_out);
  and and_16 (and_16_out, bitcross_6_p, bitcross_5_g);
  and and_17 (and_17_out, bitcross_4_g, bitcross_6_p, bitcross_5_p);
  and and_18 (and_18_out, bitcross_3_g, bitcross_6_p, bitcross_5_p, bitcross_4_p);
  and and_19 (and_19_out, bitcross_2_g, bitcross_6_p, bitcross_5_p, bitcross_4_p, bitcross_3_p);
  and and_20 (and_20_out, bitcross_1_g, bitcross_6_p, bitcross_5_p, bitcross_4_p, bitcross_3_p, bitcross_2_p);
  and and_21 (and_21_out, bitcross_6_p, bitcross_5_p, bitcross_4_p, bitcross_3_p, bitcross_2_p, bitcross_1_p, CIN);
  or or_6 (out_4[5], bitcross_6_g, and_16_out, and_17_out, and_18_out, and_19_out, and_20_out, and_21_out);
endmodule

module BitCross (
  input  A,
  input  B,
  input  Cin,
  output G,
  output P,
  output S
);

  and and_1 (G, A, B);
  or or_1 (P, A, B);
  ExactlyOne xor_1 (.out(S), .in0(Cin), .in1(A), .in2(B));
endmodule
