// Logisim project SixBitCLA.circ as structural Verilog: 3 circuits, main circuit SixBitCLA
module SixBitCLA (
  input  [5:0] A,
  input  [5:0] B,
  input  Cin,
  output [5:0] Cout,
  output [5:0] G,
  output [5:0] P,
  output [5:0] S
);

  wire and_1_out, and_2_out, and_3_out, and_4_out, and_5_out, and_6_out, and_7_out, and_8_out, and_9_out,
       and_10_out, and_11_out, and_12_out, and_13_out, and_14_out, and_15_out, and_16_out, and_17_out,
       and_18_out, and_19_out, and_20_out, and_21_out;

  MyAdder myadder_1 (.A(A[0]), .B(B[0]), .Cin(Cin), .G(G[0]), .P(P[0]), .S(S[0]));
  and and_1 (and_1_out, P[0], Cin);
  or or_1 (Cout[0], G[0], and_1_out);
  MyAdder myadder_2 (.A(A[1]), .B(B[1]), .Cin(Cout[0]), .G(G[1]), .P(P[1]), .S(S[1]));
  and and_2 (and_2_out, P[1], G[0]);
  and and_3 (and_3_out, P[1], P[0], Cin);
  MyAdder myadder_3 (.A(A[2]), .B(B[2]), .Cin(Cout[1]), .G(G[2]), .P(P[2]), .S(S[2]));
  or or_2 (Cout[1], G[1], and_2_out, and_3_out);
  and and_4 (and_4_out, P[2], G[1]);
  and and_5 (and_5_out, P[2], P[1], G[0]);
  and and_6 (and_6_out, P[2], P[1], P[0], Cin);
  MyAdder myadder_4 (.A(A[3]), .B(B[3]), .Cin(Cout[2]), .G(G[3]), .P(P[3]), .S(S[3]));
  or or_3 (Cout[2], G[2], and_4_out, and_5_out, and_6_out);
  and and_7 (and_7_out, P[3], G[2]);
  and and_8 (and_8_out, P[3], G[1], P[2]);
  and and_9 (and_9_out, P[3], G[0], P[2], P[1]);
  and and_10 (and_10_out, P[3], P[2], P[1], P[0], Cin);
  or or_4 (Cout[3], G[3], and_7_out, and_8_out, and_9_out, and_10_out);
  MyAdder myadder_5 (.A(A[4]), .B(B[4]), .Cin(Cout[3]), .G(G[4]), .P(P[4]), .S(S[4]));
  and and_11 (and_11_out, P[4], G[3]);
  and and_12 (and_12_out, P[4], G[2], P[3]);
  and and_13 (and_13_out, P[4], G[1], P[3], P[2]);
  and and_14 (and_14_out, P[4], G[0], P[3], P[2], P[1]);
  and and_15 (and_15_out, P[4], P[3], P[2], P[1], P[0], Cin);
  MyAdder myadder_6 (.A(A[5]), .B(B[5]), .Cin(Cout[4]), .G(G[5]), .P(P[5]), .S(S[5]));
  or or_5 (Cout[4], G[4], and_11_out, and_12_out, and_13_out, and_14_out, and_15_out);
  and and_16 (and_16_out, P[5], G[4]);
  and and_17 (and_17_out, G[3], P[5], P[4]);
  and and_18 (and_18_out, G[2], P[5], P[4], P[3]);
  and and_19 (and_19_out, G[1], P[5], P[4], P[3], P[2]);
  and and_20 (and_20_out, G[0], P[5], P[4], P[3], P[2], P[1]);
  and and_21 (and_21_out, P[5], P[4], P[3], P[2], P[1], P[0], Cin);
  or or_6 (Cout[5], G[5], and_16_out, and_17_out, and_18_out, and_19_out, and_20_out, and_21_out);

  // Notes on the sheet:
  //   Build your six bit CLA adder here
endmodule

module SixBitCLATest (
  input  [5:0] in_1,
  input  [5:0] in_2,
  input  in_3,
  output [5:0] out_4,
  output [5:0] out_5,
  output [5:0] out_6,
  output [5:0] out_7
);

  SixBitCLA sixbitcla_1 (.A(in_1), .B(in_2), .Cin(in_3), .Cout(out_4), .G(out_5), .P(out_6), .S(out_7));

  // Other names for the same wires on the sheet: Cout[5:0] = out_4; G[5:0] = out_5; P[5:0] = out_6; S[5:0] = out_7

  // Notes on the sheet:
  //   Build your test circuit here
endmodule

module MyAdder (
  input  A,
  input  B,
  input  Cin,
  output G,
  output P,
  output S
);

  and and_1 (G, A, B);
  or or_1 (P, A, B);
  ExactlyOne xor_1 (.out(S), .in0(Cin), .in1(A), .in2(B));
endmodule
