// Logisim project someAdder.circ as structural Verilog: 1 circuit, main circuit main
module main (
  input  [7:0] in_1,
  output out_2,
  output out_3,
  output [1:0] out_4,
  output out_5,
  output [2:0] out_6,
  output out_7,
  output out_8,
  output out_9,
  output [3:0] out_10,
  output out_11,
  output out_12,
  output [2:0] out_13,
  output [1:0] out_14,
  output out_15,
  output [2:0] out_16,
  output out_17,
  output out_18
);

  wire [7:0] not_1_out;

  assign not_1_out = ~in_1;  // NOT_Gate not_1, 8 bits wide
  Adder #(.width(1)) adder_1 (.a(not_1_out[0]), .b(not_1_out[1]), .out(out_2), .cout(out_3));  // open: cin
  Adder #(.width(1)) adder_2 (.a(not_1_out[2]), .b(not_1_out[3]), .out(out_5), .cout(out_8));  // open: cin
  Adder #(.width(1)) adder_3 (.a(not_1_out[4]), .b(not_1_out[5]), .out(out_9), .cout(out_11));  // open: cin
  Adder #(.width(1)) adder_4 (.a(not_1_out[6]), .b(not_1_out[7]), .out(out_15), .cout(out_18));  // open: cin
  Adder #(.width(2)) adder_5 (.a({out_3, out_2}), .b({out_8, out_5}), .out(out_4), .cout(out_6[2]));  // open: cin
  Adder #(.width(2)) adder_6 (.a({out_11, out_9}), .b({out_18, out_15}), .out(out_14), .cout(out_16[2]));  // open: cin
  Adder #(.width(3)) adder_7 (
    .a({out_6[2], out_4}), .b({out_16[2], out_14}), .out(out_10[2:0]), .cout(out_10[3]));  // open: cin

  assign out_6[1:0] = out_4;
  assign out_7 = out_6[2];
  assign out_12 = out_10[3];
  assign out_13 = out_10[2:0];
  assign out_16[1:0] = out_14;
  assign out_17 = out_16[2];
endmodule
