// Logisim project FiveBitAdderSubtractor.circ as structural Verilog: 3 circuits, main circuit FiveBitAdderSubtractor
module FiveBitAdderSubtractor (
  input  [4:0] A,
  input  [4:0] B,
  input  m,
  output Cout,
  output Ovf,
  output [4:0] R
);

  wire and_1_out, and_2_out, and_3_out, and_4_out, and_5_out, and_6_out, and_7_out, and_8_out, and_9_out,
       and_10_out, and_11_out, and_12_out, and_13_out, and_14_out, and_15_out, onebitaddsub_1_an,
       onebitaddsub_1_xr, onebitaddsub_2_an, onebitaddsub_2_xr, onebitaddsub_3_an, onebitaddsub_3_xr,
       onebitaddsub_4_an, onebitaddsub_4_xr, onebitaddsub_5_an, onebitaddsub_5_xr, or_1_out, or_2_out,
       or_3_out, or_4_out;

  OneBitAddSub onebitaddsub_1 (.A(A[0]), .B(B[0]), .Cin(m), .Xr(onebitaddsub_1_xr), .An(onebitaddsub_1_an));
  OneBitAddSub onebitaddsub_2 (.A(A[1]), .B(B[1]), .Cin(m), .Xr(onebitaddsub_2_xr), .An(onebitaddsub_2_an));
  OneBitAddSub onebitaddsub_3 (.A(A[2]), .B(B[2]), .Cin(m), .Xr(onebitaddsub_3_xr), .An(onebitaddsub_3_an));
  OneBitAddSub onebitaddsub_4 (.A(A[3]), .B(B[3]), .Cin(m), .Xr(onebitaddsub_4_xr), .An(onebitaddsub_4_an));
  OneBitAddSub onebitaddsub_5 (.A(A[4]), .B(B[4]), .Cin(m), .Xr(onebitaddsub_5_xr), .An(onebitaddsub_5_an));
  and and_1 (and_1_out, m, onebitaddsub_1_xr);
  and and_2 (and_2_out, onebitaddsub_2_xr, onebitaddsub_1_an);
  and and_3 (and_3_out, m, onebitaddsub_1_xr, onebitaddsub_2_xr);
  and and_4 (and_4_out, onebitaddsub_3_xr, onebitaddsub_2_xr, onebitaddsub_1_an);
  and and_5 (and_5_out, onebitaddsub_3_xr, onebitaddsub_2_an);
  and and_6 (and_6_out, onebitaddsub_4_xr, onebitaddsub_2_an, onebitaddsub_3_xr);
  and and_7 (and_7_out, onebitaddsub_4_xr, onebitaddsub_3_an);
  and and_8 (and_8_out, onebitaddsub_5_xr, onebitaddsub_4_xr, onebitaddsub_3_an);
  and and_9 (and_9_out, onebitaddsub_5_xr, onebitaddsub_4_an);
  xor xor_1 (R[0], m, onebitaddsub_1_xr);
  or or_1 (or_1_out, and_1_out, onebitaddsub_1_an);
  or or_2 (or_2_out, and_2_out, and_3_out, onebitaddsub_2_an);
  and and_10 (and_10_out, m, onebitaddsub_1_xr, onebitaddsub_2_xr, onebitaddsub_3_xr);
  and and_11 (and_11_out, m, onebitaddsub_1_xr, onebitaddsub_2_xr, onebitaddsub_3_xr, onebitaddsub_4_xr);
  and and_12 (and_12_out, onebitaddsub_1_an, onebitaddsub_2_xr, onebitaddsub_3_xr, onebitaddsub_4_xr);
  and and_13 (and_13_out, onebitaddsub_5_xr, onebitaddsub_4_xr, onebitaddsub_3_xr, onebitaddsub_2_xr, m, onebitaddsub_1_xr);
  and and_14 (and_14_out, onebitaddsub_5_xr, onebitaddsub_4_xr, onebitaddsub_3_xr, onebitaddsub_2_xr, onebitaddsub_1_an);
  and and_15 (and_15_out, onebitaddsub_5_xr, onebitaddsub_4_xr, onebitaddsub_2_an, onebitaddsub_3_xr);
  xor xor_2 (R[1], or_1_out, onebitaddsub_2_xr);
  xor xor_3 (R[2], or_2_out, onebitaddsub_3_xr);
  or or_3 (or_3_out, and_10_out, and_4_out, onebitaddsub_3_an, and_5_out);
  xor xor_4 (R[3], or_3_out, onebitaddsub_4_xr);
  or or_4 (or_4_out, and_11_out, and_12_out, and_6_out, and_7_out, onebitaddsub_4_an);
  or or_5 (Cout, onebitaddsub_5_an, and_13_out, and_14_out, and_15_out, and_8_out, and_9_out);
  xor xor_5 (R[4], or_4_out, onebitaddsub_5_xr);
  xor xor_6 (Ovf, or_4_out, Cout);

  // Notes on the sheet:
  //   Build your five bit adder subtractor here
endmodule

module FiveBitAdderSubtractorTest (
  input  [4:0] A,
  input  [4:0] B,
  input  M,
  output Cout,
  output Ovf,
  output [4:0] R
);

  FiveBitAdderSubtractor fivebitaddersubtractor_1 (.A(A), .B(B), .m(M), .Cout(Cout), .Ovf(Ovf), .R(R));

  // Notes on the sheet:
  //   Build your test circuit here
endmodule

module OneBitAddSub (
  input  A,
  input  B,
  input  Cin,
  output Xr,
  output An
);

  wire xor_1_out;

  xor xor_1 (xor_1_out, B, Cin);
  xor xor_2 (Xr, A, xor_1_out);
  and and_1 (An, xor_1_out, A);
endmodule
