// Logisim project Nifty5ALU.circ as structural Verilog: 8 circuits, main circuit Nifty5ALU
module Nifty5ALU (
  input  [4:0] A,
  input  [4:0] B,
  input  [3:0] OpCode,
  output Cout,
  output Ovf,
  output [4:0] R
);

  wire Cout_Add, Cout_ASL, M, mask, xor_1_out;
  wire [4:0] A5L, Gray, MUL3, N0T, ND, Num1, Num2, OhR, Rr, X0R;

  and and_1 (Ovf, Cout_Add, mask, Cout_ASL);
  xor xor_1 (xor_1_out, Cout_Add, Cout_ASL);
  Multiplexer #(.select(4), .enable("false")) multiplexer_1 (
    .in0(Cout_Add), .in1(Cout_Add), .in2(Cout_ASL), .in3(xor_1_out), .out(Cout), .sel(OpCode));  // open: in4, in5, in6, in7, in8, in9, in10, in11, in12, in13, in14, in15
  Multiplexer #(.select(4), .width(5), .enable("false")) multiplexer_2 (
    .in0(B), .in1(B), .in3(A5L), .out(Num2), .sel(OpCode));  // open: in2, in4, in5, in6, in7, in8, in9, in10, in11, in12, in13, in14, in15
  HexChooser hexchooser_1 (.OpCode(OpCode), .O1(M), .O3(mask));  // open: O0, O2
  Multiplexer #(.select(4), .width(5), .enable("false")) multiplexer_3 (
    .in0(A), .in1(A), .in3(A), .out(Num1), .sel(OpCode));  // open: in2, in4, in5, in6, in7, in8, in9, in10, in11, in12, in13, in14, in15
  Multiplexer #(.select(4), .width(5), .enable("false")) multiplexer_4 (
    .in0(MUL3), .in1(MUL3), .in2(A5L), .in3(MUL3), .in4(A5L), .in5(Rr), .in6(X0R), .in7(N0T), .in8(ND),
    .in9(OhR), .in10(Gray), .out(R), .sel(OpCode));  // open: in11, in12, in13, in14, in15
  FiveBitAdderSubtractor fivebitaddersubtractor_1 (.A(Num1), .B(Num2), .m(M), .Cout(Cout_Add), .R(MUL3));  // open: Ovf
  ASL asl_1 (.in_1(A), .P(A5L), .Cout(Cout_ASL));
  assign X0R = A ^ B;  // XOR_Gate xor_2, 5 bits wide
  R0R r0r_1 (.in_1(A), .out_2(Rr));
  assign N0T = A ^ {5{1'b1}};  // XOR_Gate xor_3, 5 bits wide
  ROM #(.addrWidth(5), .dataWidth(5)) rom_1 (.addr(A), .data(Gray));
  assign ND = A & B;  // AND_Gate and_2, 5 bits wide
  assign OhR = A | B;  // OR_Gate or_1, 5 bits wide

  // Other names for the same wires on the sheet: CFinal = Cout; MUL2[4:0] = A5L; SD[4:0] = MUL3

  // Notes on the sheet:
  //   Build your Nifty 5 ALU here
  //   contents of rom_1 (hex, n*v repeats v):
  //   0 1 3 2 6 17 5 4 c d f e a b 9 8 18 19 1b 1a 1e 1f 1d 1c 14 15 17 16 12 13 11 10
endmodule

module Nifty5ALUTest (
);

  Nifty5ALU nifty5alu_1 ();  // open: A, B, OpCode, Cout, Ovf, R

  // Notes on the sheet:
  //   Build your test circuit here
endmodule

module HexChooser (
  input  [3:0] OpCode,
  output O0,
  output O1,
  output O2,
  output O3
);

  wire not_1_out, not_2_out, not_3_out, not_4_out;

  not not_1 (not_1_out, OpCode[0]);
  not not_2 (not_2_out, OpCode[1]);
  not not_3 (not_3_out, OpCode[2]);
  not not_4 (not_4_out, OpCode[3]);
  and and_1 (O0, not_1_out, not_2_out, not_3_out, not_4_out);
  and and_2 (O1, OpCode[0], not_2_out, not_3_out, not_4_out);
  and and_3 (O2, OpCode[1], not_1_out, not_3_out, not_4_out);
  and and_4 (O3, OpCode[0], OpCode[1], not_3_out, not_4_out);
endmodule

module R0R (
  input  [4:0] in_1,
  output [4:0] out_2
);


  assign out_2 = {in_1[0], in_1[4:1]};
endmodule

module ASL (
  input  [4:0] in_1,
  output [4:0] P,
  output Cout
);


  assign Cout = in_1[4];
  assign P = {in_1[3:0], 1'b0};
endmodule

module FiveBitAdderSubtractor (
  input  [4:0] A,
  input  [4:0] B,
  input  m,
  output Cout,
  output Ovf,
  output [4:0] R
);

  wire and_1_out, and_2_out, and_3_out, and_4_out, and_5_out, and_6_out, and_7_out, and_8_out, and_9_out,
       and_10_out, and_11_out, and_12_out, and_13_out, and_14_out, and_15_out, onebitaddsub_1_an,
       onebitaddsub_1_xr, onebitaddsub_2_an, onebitaddsub_2_xr, onebitaddsub_3_an, onebitaddsub_3_xr,
       onebitaddsub_4_an, onebitaddsub_4_xr, onebitaddsub_5_an, onebitaddsub_5_xr, or_1_out, or_2_out,
       or_3_out, or_4_out;

  OneBitAddSub onebitaddsub_1 (.A(A[0]), .B(B[0]), .Cin(m), .Xr(onebitaddsub_1_xr), .An(onebitaddsub_1_an));
  OneBitAddSub onebitaddsub_2 (.A(A[1]), .B(B[1]), .Cin(m), .Xr(onebitaddsub_2_xr), .An(onebitaddsub_2_an));
  OneBitAddSub onebitaddsub_3 (.A(A[2]), .B(B[2]), .Cin(m), .Xr(onebitaddsub_3_xr), .An(onebitaddsub_3_an));
  OneBitAddSub onebitaddsub_4 (.A(A[3]), .B(B[3]), .Cin(m), .Xr(onebitaddsub_4_xr), .An(onebitaddsub_4_an));
  OneBitAddSub onebitaddsub_5 (.A(A[4]), .B(B[4]), .Cin(m), .Xr(onebitaddsub_5_xr), .An(onebitaddsub_5_an));
  and and_1 (and_1_out, m, onebitaddsub_1_xr);
  and and_2 (and_2_out, onebitaddsub_2_xr, onebitaddsub_1_an);
  and and_3 (and_3_out, m, onebitaddsub_1_xr, onebitaddsub_2_xr);
  and and_4 (and_4_out, onebitaddsub_3_xr, onebitaddsub_2_xr, onebitaddsub_1_an);
  and and_5 (and_5_out, onebitaddsub_3_xr, onebitaddsub_2_an);
  and and_6 (and_6_out, onebitaddsub_4_xr, onebitaddsub_2_an, onebitaddsub_3_xr);
  and and_7 (and_7_out, onebitaddsub_4_xr, onebitaddsub_3_an);
  and and_8 (and_8_out, onebitaddsub_5_xr, onebitaddsub_4_xr, onebitaddsub_3_an);
  and and_9 (and_9_out, onebitaddsub_5_xr, onebitaddsub_4_an);
  xor xor_1 (R[0], m, onebitaddsub_1_xr);
  or or_1 (or_1_out, and_1_out, onebitaddsub_1_an);
  or or_2 (or_2_out, and_2_out, and_3_out, onebitaddsub_2_an);
  and and_10 (and_10_out, m, onebitaddsub_1_xr, onebitaddsub_2_xr, onebitaddsub_3_xr);
  and and_11 (and_11_out, m, onebitaddsub_1_xr, onebitaddsub_2_xr, onebitaddsub_3_xr, onebitaddsub_4_xr);
  and and_12 (and_12_out, onebitaddsub_1_an, onebitaddsub_2_xr, onebitaddsub_3_xr, onebitaddsub_4_xr);
  and and_13 (and_13_out, onebitaddsub_5_xr, onebitaddsub_4_xr, onebitaddsub_3_xr, onebitaddsub_2_xr, m, onebitaddsub_1_xr);
  and and_14 (and_14_out, onebitaddsub_5_xr, onebitaddsub_4_xr, onebitaddsub_3_xr, onebitaddsub_2_xr, onebitaddsub_1_an);
  and and_15 (and_15_out, onebitaddsub_5_xr, onebitaddsub_4_xr, onebitaddsub_2_an, onebitaddsub_3_xr);
  xor xor_2 (R[1], or_1_out, onebitaddsub_2_xr);
  xor xor_3 (R[2], or_2_out, onebitaddsub_3_xr);
  or or_3 (or_3_out, and_10_out, and_4_out, onebitaddsub_3_an, and_5_out);
  xor xor_4 (R[3], or_3_out, onebitaddsub_4_xr);
  or or_4 (or_4_out, and_11_out, and_12_out, and_6_out, and_7_out, onebitaddsub_4_an);
  or or_5 (Cout, onebitaddsub_5_an, and_13_out, and_14_out, and_15_out, and_8_out, and_9_out);
  xor xor_5 (R[4], or_4_out, onebitaddsub_5_xr);
  xor xor_6 (Ovf, or_4_out, Cout);

  // Notes on the sheet:
  //   Build your five bit adder subtractor here
endmodule

module FiveBitAdderSubtractorTest (
  input  [4:0] A,
  input  [4:0] B,
  input  M,
  output Cout,
  output Ovf,
  output [4:0] R
);

  FiveBitAdderSubtractor fivebitaddersubtractor_1 (.A(A), .B(B), .m(M), .Cout(Cout), .Ovf(Ovf), .R(R));

  // Notes on the sheet:
  //   Build your test circuit here
endmodule

module OneBitAddSub (
  input  A,
  input  B,
  input  Cin,
  output Xr,
  output An
);

  wire xor_1_out;

  xor xor_1 (xor_1_out, B, Cin);
  xor xor_2 (Xr, A, xor_1_out);
  and and_1 (An, xor_1_out, A);
endmodule
